# Fritzing sketch led_blink (saved by Fritzing 0.9.3b)
breadboards: 1

parts:
  U2 = NodeMCU V1.0
  Part1 = Breadboard Power Supply Board SMD
  LED1 = smd LED [color="Red (633nm)" package="0805 [SMD]"]
  R1 = Resistor [tolerance=±5% resistance=1k package=THT]

nets:
  N1: U2.D0, R1.Pin_0
  N2: U2.3V3, LED1.anode
  GND: U2.GND, Part1.GND
  VIN: U2.Vin, Part1.VCC
  N3: LED1.cathode, R1.Pin_1

custom parts:
  NodeMCU V1.0: ESP8266 based NodeMCU
